# Fritzing sketch diagram (saved by Fritzing 0.9.3b)
breadboards: 2

parts:
  LCD1 = LCD screen
  S1 = Pushbutton [package="[THT]"]
  Part1 = Arduino Uno (Rev3)
  Grove1 = Grove Button  # not connected
  U1 = POT [package=alps_pot]
  J1 = Piezo Speaker
  S2 = Pushbutton [package="[THT]"]

nets:
  VSS: LCD1.VSS, LCD1.R/W, LCD1.LED-, Part1.GND, J1.pin1
  VDD: LCD1.VDD, LCD1.LED+, Part1.5V
  N1: LCD1.V0, U1.S
  N2: LCD1.RS, Part1.D7
  N3: LCD1.E, Part1.D8
  N4: LCD1.DB4, Part1.D9_PWM
  N5: LCD1.DB5, Part1.D10_PWM/SS
  N6: LCD1.DB6, Part1.D11_PWM/MOSI
  N7: LCD1.DB7, Part1.D12/MISO
  N8: S1.Pin_1, S1.Pin_2, Part1.D3_PWM
  N9: S1.Pin_3, S1.Pin_4, U1.E, S2.Pin_3, S2.Pin_4
  N10: Part1.D2, S2.Pin_1, S2.Pin_2
  N11: Part1.D5_PWM, J1.pin2
